// Logisim project ALU-Input.circ as structural Verilog: 2 circuits, main circuit ALU-Input
module ALU_Input (
  input  [31:0] in_1,
  input  constant,
  input  [15:0] in_3,
  input  Is_Inmediate,
  output [31:0] out_5
);

  wire [31:0] \const ;

  Constant_Extender constant_extender_1 (.in_1(in_3), .slti(constant), .out_3(\const ));
  Multiplexer #(.width(32), .disabled(0), .enable("false")) multiplexer_1 (
    .in0(in_1), .in1(\const ), .out(out_5), .sel(Is_Inmediate));

  // Other names for the same wires on the sheet: B[31:0] = out_5; RT[31:0] = in_1; Type_I = Is_Inmediate

  // Notes on the sheet:
  //   Input
  //   [RT]
  //   extender selector
  //   ALU-Input
  //   Output
  //   ALU-Input
endmodule

module Constant_Extender (
  input  [15:0] in_1,
  input  slti,
  output [31:0] out_3
);

  wire and_1_out;

  and and_1 (and_1_out, in_1[15], slti);
  assign out_3 = {{16{and_1_out}}, in_1};  // Bit_Extender bit_extender_1

  // Other names for the same wires on the sheet: constant[15:0] = in_1; I15 = in_1[15];
  //   extended_constant[31:0] = out_3; select = slti

  // Notes on the sheet:
  //   Input
  //   Constant
  //   addi
  //   sltiu
  //   Constant
  //   Output
endmodule
