// Logisim project ALU.circ as structural Verilog: 1 circuit, main circuit ALU
module ALU (
  input  [31:0] in_1,
  input  [31:0] in_2,
  input  [3:0] in_3,
  output [31:0] out_4,
  output [31:0] out_5
);

  wire comparator_1_lt, comparator_2_lt;
  wire [31:0] add, \and , divuHi, divuLo, muluHi, muluLo, \nor , \or , slt, stlu, sub, \xor ;

  Adder #(.width(32)) adder_1 (.a(in_1), .b(in_2), .out(add));  // open: cin, cout
  Subtractor #(.width(32)) subtractor_1 (.a(in_1), .b(in_2), .out(sub));  // open: bin, bout
  Multiplier #(.width(32)) multiplier_1 (.a(in_1), .b(in_2), .out(muluLo), .cout(muluHi));  // open: cin
  Divider #(.width(32)) divider_1 (.a(in_1), .b(in_2), .out(divuLo), .rem(divuHi));  // open: upper
  assign \and  = in_1 & in_2;  // AND_Gate and_1, 32 bits wide
  assign \or  = in_1 | in_2;  // OR_Gate or_1, 32 bits wide
  assign \nor  = ~(in_1 | in_2);  // NOR_Gate nor_1, 32 bits wide
  assign \xor  = in_1 ^ in_2;  // XOR_Gate xor_1, 32 bits wide
  Multiplexer #(.select(4), .width(32), .enable("false")) multiplexer_1 (
    .in0(add), .in1(sub), .in3(muluLo), .in5(divuLo), .in6(\and ), .in7(\or ), .in8(\nor ), .out(out_4),
    .sel(in_3));  // open: in2, in4, in9, in10, in11, in12, in13, in14, in15
  Multiplexer #(.select(2), .width(32), .disabled(0), .enable("false")) multiplexer_2 (
    .in1(divuHi), .in3(muluHi), .out(out_5), .sel(in_3[1:0]));  // open: in0, in2
  Comparator #(.width(32)) comparator_1 (.a(in_1), .b(in_2), .lt(comparator_1_lt));  // open: gt, eq
  Comparator #(.width(32), .mode("unsigned")) comparator_2 (.a(in_1), .b(in_2), .lt(comparator_2_lt));  // open: gt, eq
  assign slt = {{31{1'b0}}, comparator_1_lt};  // Bit_Extender bit_extender_1
  assign stlu = {{31{1'b0}}, comparator_2_lt};  // Bit_Extender bit_extender_2

  // Other names for the same wires on the sheet: A[31:0] = in_1; B[31:0] = in_2; F[31:0] = out_4; High[31:0] = out_5;
  //   Hi_select[1:0] = in_3[1:0]; Op[3:0] = in_3

  // Notes on the sheet:
  //   Arithmetics
  //   Inputs
  //   Logics
  //   ALU
  //   Comparison
  //   Outputs
endmodule
