// Logisim project Data Path.circ as structural Verilog: 1 circuit, main circuit Data Path
module Data_Path (
  input  in_1,
  input  [31:0] in_2,
  input  [31:0] in_3,
  input  [6:0] in_4,
  input  in_5,
  input  in_6,
  input  in_7,
  input  in_8,
  input  in_9,
  input  in_10,
  input  in_11,
  output out_12,
  output [31:0] out_13,
  output out_14,
  output [31:0] out_15,
  output out_16,
  output out_17,
  output [31:0] out_18,
  output out_19,
  output out_20,
  output [31:0] out_21,
  output [6:0] out_22,
  output [1:0] out_23,
  output out_24,
  output out_25
);

  wire instruction_decoder_1_out_19, instruction_decoder_1_out_21, pop, sw;
  wire [1:0] BC_selector;
  wire [2:0] Flag_Condition, instruction_decoder_1_out_6;
  wire [3:0] instruction_decoder_1_out_3;
  wire [4:0] instruction_decoder_1_out_10, instruction_decoder_1_selector_a, instruction_decoder_1_selector_b;
  wire [15:0] offset;
  wire [25:0] Dest;
  wire [31:0] alu_1_out_5, alu_input_1_out_5, hi_lo_1_out_5, hi_lo_1_out_6, instruction_memory_1_out_5,
       program_counter_1_p1, register_file_input_1_out_9, Rt, Rt_t;
  wire [31:7] Rs;

  Instruction_Memory instruction_memory_1 (
    .in_1(in_2), .out_5(instruction_memory_1_out_5), .en(in_9), .clk(in_11), .reset(in_10));
  Instruction_Decoder instruction_decoder_1 (
    .in_1(instruction_memory_1_out_5), .in_2(in_1), .out_3(instruction_decoder_1_out_3), .out_4(out_16),
    .out_19(instruction_decoder_1_out_19), .BC_jump_Selector(BC_selector), .Flag_Condition(Flag_Condition),
    .out_10(instruction_decoder_1_out_10), .out_6(instruction_decoder_1_out_6),
    .out_21(instruction_decoder_1_out_21), .Selector_A(instruction_decoder_1_selector_a),
    .Selector_B(instruction_decoder_1_selector_b), .out_14(offset), .out_17(Dest), .out_11(out_14),
    .out_13(out_12), .out_9(out_23), .Stop_program(out_25), .out_23(out_20), .save_word(sw),
    .keyboard(out_19), .pop(pop), .push(out_24), .out_7(out_17));
  // Program_Counter program_counter_1: pin names not known; wires that end beside it: program_counter_1_p1, in_8, in_11, in_10, out_21
  // Probe on program_counter_1_p1
  // Probe on instruction_decoder_1_selector_b
  // Probe on instruction_decoder_1_selector_a
  // Probe on out_21
  // Probe on hi_lo_1_out_5
  // Probe on instruction_decoder_1_out_10
  // Probe on offset
  Register_File_Input register_file_input_1 (
    .RF_Selector(instruction_decoder_1_out_6), .in_2(out_13), .in_3(in_11), .in_4(in_3),
    .in_5(hi_lo_1_out_6), .in_6(hi_lo_1_out_5), .Keyboard(in_4), .in_8(in_5),
    .out_9(register_file_input_1_out_9));
  // Probe on register_file_input_1_out_9
  Branch_Control branch_control_1 (
    .in_1({Rs, out_22}), .in_2(Rt_t), .in_3(out_21), .in_4(Dest), .in_5(offset),
    .Fag_Condition(Flag_Condition), .Jump_Selector(BC_selector), .out_8(program_counter_1_p1));
  // Probe on hi_lo_1_out_6
  // Register_File register_file_1: pin names not known; wires that end beside it: register_file_input_1_out_9, instruction_decoder_1_out_10, in_7, in_10, pop, out_24, in_8, in_11, instruction_decoder_1_selector_a, instruction_decoder_1_selector_b, {Rs, out_22}, Rt, out_15
  // Probe on {Rs, out_22}
  // Probe on Rt
  ALU_Input alu_input_1 (
    .in_1(Rt), .constant(instruction_decoder_1_out_19), .in_3(offset),
    .Is_Inmediate(instruction_decoder_1_out_21), .out_5(alu_input_1_out_5));
  // Probe on alu_input_1_out_5
  Multiplexer #(.width(32), .disabled(0), .enable("false")) multiplexer_1 (
    .in0({Rs, out_22}), .in1(Rt_t), .out(out_18), .sel(sw));
  // Probe on out_13
  ALU alu_1 (
    .in_1({Rs, out_22}), .in_2(alu_input_1_out_5), .in_3(instruction_decoder_1_out_3), .out_4(out_13),
    .out_5(alu_1_out_5));
  Hi_Lo hi_lo_1 (
    .in_1(out_13), .in_2(alu_1_out_5), .in_3(in_6), .in_4(in_11), .out_5(hi_lo_1_out_5), .out_6(hi_lo_1_out_6));

  // Other names for the same wires on the sheet: ALU_output[31:0] = out_13; clk = in_11; halt = out_25;
  //   HI_LO_en = in_6; IM_en = in_9; instruction[31:0] = in_2; is_inst = in_1; kbd = out_19; KBD_avail = in_5;
  //   KBD_data[6:0] = in_4; MA_input_select[1:0] = out_23; PC[31:0] = out_21; PC_en = in_8; push = out_24;
  //   RAM_data[31:0] = in_3; RAM_input[31:0] = out_18; read_R = out_14; reset = in_10; RF_en = out_17; RF_R_W = in_7;
  //   Rs[6:0] = out_22; TTY_DATA[6:0] = out_22; SP[31:0] = out_15; tty = out_20; use_HI_LO = out_16; write_R = out_12

  // Notes on the sheet:
  //   Inputs
  //   Data Path
  //   Outputs
endmodule
